# Fritzing sketch electronics0 - Copie (saved by Fritzing 1.0.4)
circuit board: 8.46667cm x 5.64444cm
stripboards: 1

parts:
  Mod1 = Amica NodeMCU DEVKIT 1.0
  Servo = Basic Servo
  Yumo-enc1 = YumoE6B2
  H_ENCODER = male pin header, 4 pins [form="♂ (male)"]
  H_OPTICAL = male pin header, 3 pins [form="♂ (male)"]
  J7 = female pin header, 2 pins [form="♀ (female)"]
  J9 = female pin header, 2 pins [form="♀ (female)"]
  J8 = female pin header, 3 pins [form="♀ (female)"]
  D0 = female pin header, 1 pin [form="♀ (female)"]
  J3 = Dagu DGServo 9g header connector (female) [package=THT]
  H_PWR = Screw terminal - 2 pins [package=THT]
  Optical = KY-010 Photo Interrupter Module [package="Breakout board"]
  M1 = RioRand LM2596  # not connected
  U1 = NodeMCU V3.0  # not connected

nets:
  3.3V: Mod1.pin1, Mod1.pin_10, Mod1.pin_26, H_OPTICAL.pin2, J8.pin2, Optical.Vin
  GND: Mod1.pin2, Mod1.pin_9, Mod1.pin_29, Servo.gnd, Yumo-enc1.GND, H_ENCODER.pin2, H_OPTICAL.pin1, J7.pin1, J8.pin3, J3.gnd, H_PWR.pin2, Optical.-
  N1: Mod1.pin6, Yumo-enc1.B, H_ENCODER.pin3, J9.pin2
  N2: Mod1.pin7, Yumo-enc1.A, H_ENCODER.pin4, J9.pin1
  N3: Mod1.pin_11, H_OPTICAL.pin3, J8.pin1, Optical.S
  N4: Mod1.pin_14, Servo.pulse, D0.pin1, J3.pulse
  6V: Mod1.pin_30, Servo.vcc, Yumo-enc1.V, H_ENCODER.pin1, J7.pin2, J3.Vcc, H_PWR.pin1

custom parts:
  KY-010 Photo Interrupter Module: Photo Interrupter Module Keyes KY-010 for Arduino, will trigger a signal when light between the sensor's gap is blocked.
  NodeMCU V3.0: NodeMcu V3 Lua WIFI Development Board
