# Fritzing sketch electronics0 (saved by Fritzing 1.0.4)
circuit board: 8.46667cm x 5.64444cm
stripboards: 1

parts:
  Servo = Basic Servo
  Yumo-enc1 = YumoE6B2
  H_OPTICAL = male pin header, 3 pins [form="♂ (male)"]
  Optical = KY-010 Photo Interrupter Module [package="Breakout board"]
  M1 = RioRand LM2596
  ESP = NodeMCU V3.0
  H_ESPR = female pin header, 15 pins [form="♀ (female)"]
  H_ESPL = female pin header, 15 pins [form="♀ (female)"]
  H_GND_IN = male pin header, 1 pin [form="♂ (male)"]
  H_VCC_IN = male pin header, 1 pin [form="♂ (male)"]
  H_GND_OUT = male pin header, 1 pin [form="♂ (male)"]
  H_VCC_OUT = male pin header, 1 pin [form="♂ (male)"]
  J3 = Dagu DGServo 9g header (male) [package=THT]
  H_ENCODER = male pin header, 5 pins [form="♂ (male)"]

nets:
  GND: Servo.gnd, Yumo-enc1.GND, H_OPTICAL.pin1, Optical.-, M1.Pin_4, ESP.GND#6, ESP.GND#13, ESP.GND#16, ESP.GND#33, H_ESPR.pin7, H_ESPR.pin14, H_ESPL.pin10, H_ESPL.pin14, H_GND_OUT.pin1, J3.gnd, H_ENCODER.pin1, H_ENCODER.pin2
  6V: Servo.vcc, Yumo-enc1.V, M1.Pin_3, ESP.Vin, H_ESPL.pin15, H_VCC_OUT.pin1, J3.Vcc, H_ENCODER.pin3
  N1: Servo.pulse, ESP.D1, H_ESPR.pin2, J3.pulse
  N2: Yumo-enc1.A, ESP.D6, H_ESPR.pin9, H_ENCODER.pin5
  N3: Yumo-enc1.B, ESP.D7, H_ESPR.pin10, H_ENCODER.pin4
  3.3V: H_OPTICAL.pin2, Optical.Vin, ESP.3V3, H_ESPR.pin6, H_ESPR.pin15, H_ESPL.pin11
  N4: H_OPTICAL.pin3, Optical.S, ESP.D4, H_ESPR.pin5
  N5: M1.Pin_1, H_VCC_IN.pin1
  N6: M1.Pin_2, H_GND_IN.pin1
  N7: ESP.D0, H_ESPR.pin1
  N8: ESP.D2, H_ESPR.pin3
  N9: ESP.D3, H_ESPR.pin4
  N10: ESP.D5, H_ESPR.pin8
  N11: ESP.D8, H_ESPR.pin11
  N12: ESP.RX, H_ESPR.pin12
  N13: ESP.TX, H_ESPR.pin13
  N14: ESP.RST, H_ESPL.pin13
  N15: ESP.EN, H_ESPL.pin12
  N16: ESP.CLK, H_ESPL.pin9
  N17: ESP.SD0, H_ESPL.pin8
  N18: ESP.CMD, H_ESPL.pin7
  N19: ESP.SD1, H_ESPL.pin6
  N20: ESP.SD2, H_ESPL.pin5
  N21: ESP.SD3, H_ESPL.pin4
  N22: ESP.VU, H_ESPL.pin3
  N23: ESP.GND#41, H_ESPL.pin2
  N24: ESP.A0, H_ESPL.pin1

notes:
  ⨂

custom parts:
  KY-010 Photo Interrupter Module: Photo Interrupter Module Keyes KY-010 for Arduino, will trigger a signal when light between the sensor's gap is blocked.
  NodeMCU V3.0: NodeMcu V3 Lua WIFI Development Board
